# Fritzing sketch environmentmonitor (saved by Fritzing 0.9.3b)
breadboards: 1

parts:
  Part1 = Arduino Leonardo (Rev3b)
  Part2 = Adafruit SGP30 Gas Sensor
  Part3 = Adafruit TSL2591 [part_number="Adafruit #1980"]
  DHT1 = DHT22 Humidity and Temperature Sensor
  PART1 = Sound Detector

nets:
  N1: Part1.D4/A6, DHT1.DATA
  3V3: Part1.3V3, Part3.VIN, PART1.VCC
  5V: Part1.5V, Part2.VIN, DHT1.VDD
  GND: Part1.GND, Part2.GND, Part3.GND, DHT1.GND, PART1.GND
  N2: Part1.A3, PART1.ENVELOPE
  N3: Part1.SDA, Part2.SDA, Part3.SDA
  N4: Part1.SCL, Part2.SCL, Part3.SCL

custom parts:
  Adafruit TSL2591: When the future is dazzlingly-bright, this ultra-high-range luminosity sensor will help you measure it. The TSL2591 luminosity sensor is an advanced digital light sensor, ideal for use in a wide range of light situations. Compared to low cost CdS cells, this sensor is more precise, allowing for exact lux calculations and can be configured for different gain/timing ranges to detect light ranges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
  Sound Detector: Electret microphone with multiple outputs. - First output is the actual audio - Second output is the amplitude envelope - Third output is a binary "sound present" indication - high while sound is present, low otherwise. Visit sparkfun.com for more documentations.
